// Logisim project fibonacci.circ as structural Verilog: 3 circuits, main circuit main
module main (
);

  wire spliter_1_out_2;
  wire [15:0] cdm_16_1_t;

  CdM_16 cdm_16_1 (.t(cdm_16_1_t));
  LED led_1 (.in(spliter_1_out_2));
  spliter spliter_1 (.out_2(spliter_1_out_2), .in_1(cdm_16_1_t));
endmodule

module CdM_16 (
  output [15:0] t
);

  wire cdm_16_1_p1, cdm_16_1_p3, cdm_16_1_p4, cdm_16_1_p7, code, data, not_1_out, read_write, word;
  wire [15:0] cdm_16_1_p8, cdm_16_1_p9, controlled_buffer_1_out;

  // Debugger debugger_1: pin names not known
  // logisim_cdm_emulator_0_2_1_CdM_16 cdm_16_1: pin names not known; wires that end beside it: cdm_16_1_p1, t, cdm_16_1_p3, cdm_16_1_p4, read_write, word, cdm_16_1_p7, cdm_16_1_p8, cdm_16_1_p9
  Clock clock_1 (.out(cdm_16_1_p1));
  assign controlled_buffer_1_out = not_1_out ? cdm_16_1_p8 : 16'bz;  // Controlled_Buffer controlled_buffer_1
  not not_1 (not_1_out, read_write);
  assign cdm_16_1_p9 = read_write ? controlled_buffer_1_out : 16'bz;  // Controlled_Buffer controlled_buffer_2
  Decoder #(.disabled(0)) decoder_1 (.out0(code), .out1(data), .sel(cdm_16_1_p3), .en(cdm_16_1_p4));
  // ROM rom_1: pin names not known; wires that end beside it: cdm_16_1_p7, code, word, controlled_buffer_1_out
  // RAM ram_1: pin names not known; wires that end beside it: cdm_16_1_p7, word, data, cdm_16_1_p1, read_write, controlled_buffer_1_out
endmodule

module spliter (
  input  [15:0] in_1,
  output out_2
);


  assign out_2 = in_1[0];
endmodule
